# Fritzing sketch nodemcuv3_ir-remote (saved by Fritzing 0.9.3b)
circuit board: 8.46667cm x 5.64444cm
breadboards: 1

parts:
  ESP8266_Node_MCU = NodeMCU V3.0
  IR-Diode = LTE-302 [package=lte-302]
  Q1 = NPN-Transistor [package="SOT-23 [SMD]"]
  R1 = Resistor [tolerance=±5% resistance=15 package=THT]
  TSOP31240 = TSOP312.., 314.. [package=THT]

nets:
  N1: ESP8266_Node_MCU.D0, R1.Pin_0
  N2: ESP8266_Node_MCU.3V3, IR-Diode.A, TSOP31240.Vs
  N3: ESP8266_Node_MCU.GND#6, ESP8266_Node_MCU.GND#13, ESP8266_Node_MCU.GND#16, ESP8266_Node_MCU.GND#33
  N4: ESP8266_Node_MCU.D5, TSOP31240.Data
  N5: ESP8266_Node_MCU.GND#41, Q1.2, TSOP31240.GND
  N6: IR-Diode.C, Q1.1
  N7: Q1.0, R1.Pin_1

custom parts:
  NodeMCU V3.0: ESP8266 based NodeMCU
